// Logisim project 171044073.circ as structural Verilog: 1 circuit, main circuit main
// nunber
module main (
  input  [4:0] Number,
  input  in_2
);

  wire xnor_1_out, xnor_2_out, xnor_3_out;

  xnor xnor_1 (xnor_1_out, Number[4], Number[3]);
  xnor xnor_2 (xnor_2_out, xnor_1_out, xnor_3_out);
  xnor xnor_3 (xnor_3_out, Number[2], Number[1]);
  or or_1 (in_2, xnor_2_out, Number[0]);
endmodule
